// Logisim project alu.circ as structural Verilog
module alu (
  input  [31:0] A,
  input  [31:0] B,
  input  [3:0] ALUSel,
  output [31:0] Result,
  output [31:0] out_5
);

  wire [31:0] add, and1, bsel13, divu8, mulh14, mulhu11, mult10, or2, remu9, sll6, slt7, sra5, srl4, sub12,
       xor3;

  bsel13 bsel13_1 (.A(A), .B(B), .bsel13(bsel13));
  mulh14 mulh14_1 (.A(A), .B(B), .mulh14(mulh14));
  Adder #(.width(32)) adder_1 (.a(A), .b(B), .out(add));  // open: cin, cout
  assign and1 = A & B;  // AND_Gate and_1, 32 bits wide
  assign or2 = A | B;  // OR_Gate or_1, 32 bits wide
  xor3 xor3_1 (.A(A), .B(B), .xor3(xor3));
  srl4 srl4_1 (.A(A), .B(B), .srl4(srl4));
  sra5 sra5_1 (.A(A), .B(B), .sra5(sra5));
  sll6 sll6_1 (.A(A), .B(B), .sll6(sll6));
  slt7 slt7_1 (.A(A), .B(B), .slt7(slt7));
  divu8 divu8_1 (.A(A), .B(B), .divu8(divu8));
  remu9 remu9_1 (.A(A), .B(B), .remu9(remu9));
  mult10 mult10_1 (.A(A), .B(B), .mult10(mult10));
  mulhu11 mulhu11_1 (.A(A), .B(B), .mulhu(mulhu11));
  sub12 sub12_1 (.A(A), .B(B), .sub12(sub12));
  Multiplexer #(.select(4), .width(32), .enable("false")) multiplexer_1 (
    .in0(add), .in1(and1), .in2(or2), .in3(xor3), .in4(srl4), .in5(sra5), .in6(sll6), .in7(slt7),
    .in8(divu8), .in9(remu9), .in10(mult10), .in11(mulhu11), .in12(sub12), .in13(bsel13), .in14(mulh14),
    .out(out_5), .sel(ALUSel));  // open: in15

  assign Result = out_5;

  // Notes on the sheet:
  //   INPUTS to your circuit
  //   DON'T CHANGE THE LOCATIONS OF THE INPUTS AND OUTPUTS!
  //   OUTPUT from your circuit
endmodule

module xor3 (
  input  [31:0] A,
  input  [31:0] B,
  output [31:0] xor3
);

  wire [31:0] and_1_out, and_2_out, not_1_out, not_2_out;

  assign not_1_out = ~A;  // NOT_Gate not_1, 32 bits wide
  assign not_2_out = ~B;  // NOT_Gate not_2, 32 bits wide
  assign and_1_out = not_1_out & B;  // AND_Gate and_1, 32 bits wide
  assign and_2_out = not_2_out & A;  // AND_Gate and_2, 32 bits wide
  assign xor3 = and_1_out | and_2_out;  // OR_Gate or_1, 32 bits wide
endmodule

module srl4 (
  input  [31:0] A,
  input  [31:0] B,
  output [31:0] srl4
);

  Shifter #(.width(32), .shift("lr")) shifter_1 (.in(A), .\dist (B[4:0]), .out(srl4));
endmodule

module sra5 (
  input  [31:0] A,
  input  [31:0] B,
  output [31:0] sra5
);

  Shifter #(.width(32), .shift("ar")) shifter_1 (.in(A), .\dist (B[4:0]), .out(sra5));
endmodule

module sll6 (
  input  [31:0] A,
  input  [31:0] B,
  output [31:0] sll6
);

  Shifter #(.width(32)) shifter_1 (.in(A), .\dist (B[4:0]), .out(sll6));
endmodule

module slt7 (
  input  [31:0] A,
  input  [31:0] B,
  output [31:0] slt7
);

  wire comparator_1_lt;

  Comparator #(.width(32)) comparator_1 (.a(A), .b(B), .lt(comparator_1_lt));  // open: gt, eq
  assign slt7 = {{31{1'b0}}, comparator_1_lt};  // Bit_Extender bit_extender_1
endmodule

module divu8 (
  input  [31:0] A,
  input  [31:0] B,
  output [31:0] divu8
);

  Divider #(.width(32)) divider_1 (.a(A), .b(B), .out(divu8));  // open: upper, rem
endmodule

module remu9 (
  input  [31:0] A,
  input  [31:0] B,
  output [31:0] remu9
);

  Divider #(.width(32)) divider_1 (.a(A), .b(B), .rem(remu9));  // open: out, upper
endmodule

module mult10 (
  input  [31:0] A,
  input  [31:0] B,
  output [31:0] mult10
);

  Multiplier #(.width(31)) multiplier_1 (.a(A[30:0]), .b(B[30:0]), .out(mult10[30:0]));  // open: cin, cout
  xor xor_1 (mult10[31], A[31], B[31]);
endmodule

module mulhu11 (
  input  [31:0] A,
  input  [31:0] B,
  output [31:0] mulhu
);

  Multiplier #(.width(32)) multiplier_1 (.a(A), .b(B), .cout(mulhu));  // open: out, cin
endmodule

module sub12 (
  input  [31:0] A,
  input  [31:0] B,
  output [31:0] sub12
);

  Subtractor #(.width(32)) subtractor_1 (.a(A), .b(B), .out(sub12));  // open: bin, bout
endmodule

module bsel13 (
  input  [31:0] A,
  input  [31:0] B,
  output [31:0] bsel13
);

  Multiplexer #(.width(32), .enable("false")) multiplexer_1 (.in0(A), .in1(B), .out(bsel13), .sel(1'b1));
endmodule

module mulh14 (
  input  [31:0] A,
  input  [31:0] B,
  output [31:0] mulh14
);

  wire xor_1_out;
  wire [31:0] compli_1_out_2, compli_2_out_2, multiplexer_1_out, multiplexer_2_out, multiplier_1_cout,
       not_1_out;

  compli compli_1 (.IN1(A), .out_2(compli_1_out_2));
  compli compli_2 (.IN1(B), .out_2(compli_2_out_2));
  Multiplexer #(.width(32), .enable("false")) multiplexer_1 (
    .in0(A), .in1(compli_1_out_2), .out(multiplexer_1_out), .sel(A[31]));
  Multiplexer #(.width(32), .enable("false")) multiplexer_2 (
    .in0(B), .in1(compli_2_out_2), .out(multiplexer_2_out), .sel(B[31]));
  Multiplier #(.width(32)) multiplier_1 (
    .a(multiplexer_1_out), .b(multiplexer_2_out), .cout(multiplier_1_cout));  // open: out, cin
  assign not_1_out = ~multiplier_1_cout;  // NOT_Gate not_1, 32 bits wide
  xor xor_1 (xor_1_out, A[31], B[31]);
  Multiplexer #(.width(32), .enable("false")) multiplexer_3 (
    .in0(multiplier_1_cout), .in1(not_1_out), .out(mulh14), .sel(xor_1_out));
endmodule

module compli (
  input  [31:0] IN1,
  output [31:0] out_2
);

  wire [31:0] not_1_out;

  assign not_1_out = ~IN1;  // NOT_Gate not_1, 32 bits wide
  Adder #(.width(32)) adder_1 (.a(not_1_out), .b(32'h1), .out(out_2));  // open: cin, cout
endmodule
